// Logisim project Logisim DECO Work.circ as structural Verilog: 1 circuit, main circuit main
module main (
  input  A,
  input  B,
  input  A_2,
  input  B_2,
  input  A_3,
  input  B_3,
  input  Cin,
  input  I0,
  input  I1,
  input  I2,
  input  I3,
  input  S0,
  input  S1,
  output F,
  output Sum,
  output Carry,
  output Sum_2,
  output Cout,
  output Y
);

  wire and_2_out, and_3_out, and_4_out, and_5_out, and_6_out, and_7_out, nand_1_out, nand_2_out, nand_3_out,
       not_1_out, not_2_out, xor_1_out;

  not not_1 (not_1_out, S0);
  not not_2 (not_2_out, S1);
  nand nand_1 (nand_1_out, A, B);
  xor xor_1 (xor_1_out, A_3, B_3);
  nand nand_2 (nand_2_out, A, nand_1_out);
  nand nand_3 (nand_3_out, nand_1_out, B);
  xor xor_2 (Sum, A_2, B_2);
  and and_1 (Carry, B_2, A_2);
  and and_2 (and_2_out, A_3, B_3);
  xor xor_3 (Sum_2, xor_1_out, Cin);
  and and_3 (and_3_out, xor_1_out, Cin);
  and and_4 (and_4_out, I0, S0, S1);
  and and_5 (and_5_out, I1, not_1_out, S1);
  and and_6 (and_6_out, I2, not_2_out, S1);
  and and_7 (and_7_out, I3, not_1_out, not_2_out);
  nand nand_4 (F, nand_2_out, nand_3_out);
  or or_1 (Cout, and_3_out, and_2_out);
  nor nor_1 (Y, and_4_out, and_5_out, and_6_out, and_7_out);

  // Notes on the sheet:
  //   Half Adder
  //   Full Adder
  //   Mux 4 to 1
  //   XOR Gate Using NAND Gates
  //   (AB)'
  //   A'B
  //   AB'
  //   = A'B+AB'
endmodule
